# Fritzing sketch Sketch (saved by Fritzing 0.9.3b)
breadboards: 1

parts:
  R4 = Resistor [tolerance=±5% resistance=220 package=THT]
  R5 = Resistor [tolerance=±5% resistance=220 package=THT]
  R6 = Resistor [tolerance=±5% resistance=220 package=THT]
  LED4 = LED - 5mm [color="Green (555nm)" package="5 mm [THT]"]
  LED5 = LED - 5mm [color="Green (555nm)" package="5 mm [THT]"]
  LED6 = LED - 5mm [color="Green (555nm)" package="5 mm [THT]"]
  U1 = POT [package=pot_mammoth]
  R7 = Resistor [tolerance=±5% resistance=220 package=THT]
  R8 = Resistor [tolerance=±5% resistance=220 package=THT]
  R9 = Resistor [tolerance=±5% resistance=220 package=THT]  # not connected
  R10 = Resistor [tolerance=±5% resistance=220 package=THT]  # not connected
  U2 = 7-SEGMENT-DISPLAY [package=7-segment-display]
  R11 = Resistor [tolerance=±5% resistance=220 package=THT]
  R12 = Resistor [tolerance=±5% resistance=220 package=THT]
  R13 = Resistor [tolerance=±5% resistance=220 package=THT]
  Bauteil1 = Arduino Uno (Rev3) - ICSP
  S3 = Pushbutton [package="[SMD]"]
  R14 = Resistor [tolerance=±5% resistance=10k package=THT]
  LED7 = RGB LED (com. anode, rbg) [package="5 mm [THT]"]
  R15 = Resistor [tolerance=±5% resistance=220 package=THT]
  R16 = Resistor [tolerance=±5% resistance=220 package=THT]
  LED8 = LED - 5mm [color="Orange (605nm)" package="5 mm [THT]"]
  R17 = Resistor [tolerance=±5% resistance=220 package=THT]

nets:
  N1: R4.Pin_0, Bauteil1.D2
  N2: R4.Pin_1, LED4.anode
  N3: R5.Pin_0, Bauteil1.D3_PWM
  N4: R5.Pin_1, LED5.anode
  N5: R6.Pin_0, Bauteil1.D4
  N6: R6.Pin_1, LED6.anode
  N7: LED4.cathode, LED5.cathode
  N8: LED6.cathode, U1.E, U2.C, R14.Pin_1
  N9: U1.S, R17.Pin_1
  N10: U1.A, Bauteil1.A0
  N11: R7.Pin_0, Bauteil1.D8
  N12: R7.Pin_1, U2.E
  N13: R8.Pin_0, Bauteil1.D9_PWM
  N14: R8.Pin_1, U2.G
  N15: U2.D, R12.Pin_1
  N16: U2.G1, R11.Pin_1
  N17: U2.DP, R13.Pin_1
  N18: R11.Pin_0, Bauteil1.D13/SCK
  N19: R12.Pin_0, Bauteil1.D12/MISO
  N20: R13.Pin_0, Bauteil1.D0/RX
  N21: Bauteil1.D1/TX, LED8.anode
  N22: Bauteil1.D5_PWM, S3.Pin_1, S3.Pin_2, R14.Pin_0
  N23: Bauteil1.D6_PWM, R16.Pin_0
  N24: Bauteil1.D7, R15.Pin_0
  N25: S3.Pin_3, S3.Pin_4
  N26: LED7.blue_cathode, R16.Pin_1
  N27: LED7.green_cathode, R15.Pin_1
  N28: LED8.cathode, R17.Pin_0
